# Fritzing sketch Sniffer (saved by Fritzing 0.9.2b)
breadboards: 1

parts:
  U1 = NodeMCU V3.0
  LED2 = smd LED [color="Red (633nm)" package="1206 [SMD]"]
  LED3 = smd LED [color="Green (570nm)" package="1206 [SMD]"]
  R1 = Resistor [tolerance=±5% resistance=220 package="2512 [SMD]"]
  R2 = Resistor [tolerance=±5% resistance=220 package="2512 [SMD]"]

nets:
  N1: U1.D2, R2.Pin_1
  N2: U1.GND#6, U1.GND#13, U1.GND#16, LED2.cathode, LED3.cathode
  N3: U1.D5, R1.Pin_1
  N4: U1.S3, U1.VU
  N5: LED2.anode, R1.Pin_0
  N6: LED3.anode, R2.Pin_0

notes:
  DHT11
  NovaFitness SDS011
  Reset wires

custom parts:
  NodeMCU V3.0: ESP8266 based NodeMCU
